# Fritzing sketch Motor test bench (saved by Fritzing 0.9.3b)

parts:
  Componente1 = Arduino Uno (Rev3) - ICSP
  Componente3 = HX711 Module
  Load_Cell1 = Load Cell
  M1 = DC Motor
  Q1 = PHOTOTRANSISTOR REFLECTIVE OBJECT SENSOR [package=qrb1114-side]
  R1 = Resistor [tolerance=±5% resistance=1k package="0603 [SMD]"]
  DRV_1 = DRV 8825 Stepper Motor Carrier, High Current [part_number="DRV 8825"]
  M2 = Stepper Motor - Bipolar
  KY-1 = Keyes Relay [package=THT]
  C1 = Electrolytic Capacitor [capacitance=1μF package="0405 [SMD, electrolytic]"]

nets:
  N1: Componente1.D10_PWM/SS, Componente3.DO/RX
  N2: Componente1.D11_PWM/MOSI, Componente3.CK/TX
  GND: Componente1.GND, Componente3.GND, Q1.C, Q1.K, DRV_1.GROUND_LOG, KY-1.ground
  N3: Componente1.D3_PWM, Q1.A
  N4: Componente1.D4, KY-1.signal
  N5: Componente1.D6_PWM, DRV_1.DIRECTION
  N6: Componente1.D7, DRV_1.STEP
  N7: Componente1.IOREF, Componente3.VCC
  N8: Componente1.5V, R1.Pin_1
  N9: Componente1.VIN, DRV_1.RESET, DRV_1.SLEEP, KY-1.power
  N10: Componente3.E+, Load_Cell1.wire1
  N11: Componente3.E-, Load_Cell1.wire2
  N12: Componente3.A+, Load_Cell1.wire3
  N13: Componente3.A-, Load_Cell1.wire4
  N14: M1.pin_1, DRV_1.GROUND_ST/_MT, C1.+
  N15: M1.pin_2, KY-1.NO
  N16: Q1.E, R1.Pin_0
  N17: DRV_1.VOLTAGE_ST/_MT, KY-1.C, C1.-
  N18: DRV_1.OUT_2B, M2.A
  N19: DRV_1.OUT_2A, M2.C
  N20: DRV_1.OUT_1A, M2.B
  N21: DRV_1.OUT_1B, M2.D

notes:
  12V

custom parts:
  HX711 Module: HX711 is a precision 24-bit analog-to-digital converter (ADC) designed for weigh scales and industrial control applications to interface directly with a bridge sensor.
  Load Cell: A rectangle load cell/weighting pressure Sensor with four wires - Red, white, black, green. Normally corresponding with E+, E-, A+, A- respectively.
  Keyes Relay: The Keyes 5V relay module is suitable for SCM development, home appliance control. It uses a 5V~12V TIL control signal which can control DC / AC signal.
